# Fritzing sketch Arduino VFD (saved by Fritzing 0.9.3b)

parts:
  J1 = male pin header, 4 pins [form="♂ (male)"]
  Part1 = Arduino Nano (Rev3.0)
  X1 = DB9 Connector [package=db9]
  JACK1 = 2.1mm Barrel Jack with Terminal Block
  J3 = female pin header, 8 pins [form="♀ (female)"]

nets:
  N1: J1.pin1, Part1.5V
  N2: J1.pin3, Part1.D9
  N3: J1.pin4, Part1.GND
  N4: X1.5, JACK1.NEG, J3.pin1, J3.pin6, J3.pin8
  N5: X1.8, J3.pin3
  N6: JACK1.POS, J3.pin7

notes:
  12V DC
  TTL RS232 Convertor
  RS232 pinout:
  1 DCD (not used)
  2 Rx
  3 Tx (not used)
  4 DTR (not used)
  5 GND
  6 DSR (not used)
  7 RTS (not used)
  8 CTS (not used)
  9 RI (not used)
  VFD Display
  MAX232 chip converts serial signals from TTL (0 - 5V) to RS232 (+15V - -15V)
  AltSoftSerial library uses Pin 9 to transmit serial data
  DM-D110 RJ45 Connector pinout:
  1 GND
  2 Tx (not used)
  3 Rx (to MAX232 Tx)
  4 DSR (not used)
  5 DTR (not used)
  6 GND
  7 V+ (to 12V)
  8 GND
